# Fritzing sketch L298N (saved by Fritzing 0.9.3b)

parts:
  Part1 = Arduino Uno (Rev3)
  M1 = DC Motor
  L298N1 = L298N DC motor driver
  12V1 = 2.1mm Barrel Jack with Terminal Block

nets:
  N1: Part1.D8, L298N1.IN1
  N2: Part1.D9_PWM, L298N1.ENA
  GND: Part1.GND, L298N1.GND, 12V1.NEG
  N3: Part1.D7, L298N1.IN2
  N4: M1.pin_1, L298N1.OUT2
  N5: M1.pin_2, L298N1.OUT1
  N6: L298N1.12V, 12V1.POS

custom parts:
  L298N DC motor driver: 2x DC motor driver with 78M05 positive voltage regulator (7..35 V) L298N: max 46 V, 2 A Set 5 V Enable jumper to enable 5 V regultor (needed for the L298N) and +5 V output at screw terminal or supply external +5 V at screw terminal Set ENA and/or ENB to +5 V to enable motor permanently or supply ENA and/or ENB with PWM signal IN1 and IN2 set rotation directory for motor A (OUT1/OUT2) IN2 and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
